// Logisim project projeto.circ as structural Verilog: 2 circuits, main circuit main
module main (
  input  Start,
  input  PG,
  input  CH,
  input  RO,
  input  CQ,
  input  EB,
  output E2,
  output E1,
  output E0
);

  wire and_1_out, Clock_out, Decodificador_0_9_2_a_2, Decodificador_0_9_2_b_2, Decodificador_0_9_2_c_2,
       Decodificador_0_9_2_d_2, Decodificador_0_9_2_dp, Decodificador_0_9_2_e, Decodificador_0_9_2_f,
       Decodificador_0_9_2_g, Decodificador_0_9_a_2, Decodificador_0_9_b_2, Decodificador_0_9_c_2,
       Decodificador_0_9_d_2, Decodificador_0_9_dp, Decodificador_0_9_e, Decodificador_0_9_f,
       Decodificador_0_9_g, MEF_Principal_alarme, MEF_Principal_ev, MEF_Principal_motor, MEF_Principal_ve;

  Clock Clock (.out(Clock_out));
  mef_principal_main MEF_Principal (
    .Clock(Clock_out), .Start(Start), .PG(PG), .CH(CH), .RO(RO), .CQ(CQ), .EB(EB), .E2(E2), .E1(E1), .E0(E0),
    .MOTOR(MEF_Principal_motor), .EV(MEF_Principal_ev), .VE(MEF_Principal_ve), .ALARME(MEF_Principal_alarme));
  and and_1 (and_1_out, E2, E1, ~E0);  // AND_Gate
  decod_num_0_9 Decodificador_0_9 (
    .A_2(Decodificador_0_9_a_2), .B_2(Decodificador_0_9_b_2), .C_2(Decodificador_0_9_c_2),
    .D_2(Decodificador_0_9_d_2), .E(Decodificador_0_9_e), .F(Decodificador_0_9_f), .G(Decodificador_0_9_g),
    .DP(Decodificador_0_9_dp));  // open: a, b, c, d
  decod_num_0_9 Decodificador_0_9_2 (
    .A_2(Decodificador_0_9_2_a_2), .B_2(Decodificador_0_9_2_b_2), .C_2(Decodificador_0_9_2_c_2),
    .D_2(Decodificador_0_9_2_d_2), .E(Decodificador_0_9_2_e), .F(Decodificador_0_9_2_f),
    .G(Decodificador_0_9_2_g), .DP(Decodificador_0_9_2_dp));  // open: a, b, c, d
  LED Motor (.in(MEF_Principal_motor));
  LED EV (.in(MEF_Principal_ev));
  LED VE (.in(MEF_Principal_ve));
  LED Alarme (.in(MEF_Principal_alarme));
  LED u_PG (.in(PG));
  LED u_CH (.in(CH));
  LED u_RO (.in(RO));
  LED u_CQ (.in(CQ));
  LED u_EB (.in(EB));
  LED u_Start (.in(Start));
  _7_Segment_Display #(.active("false")) u_7_segment_display_1 (
    .g(Decodificador_0_9_g), .f(Decodificador_0_9_f), .a(Decodificador_0_9_a_2), .b(Decodificador_0_9_b_2),
    .e(Decodificador_0_9_e), .d(Decodificador_0_9_d_2), .c(Decodificador_0_9_c_2), .dp(Decodificador_0_9_dp));
  _7_Segment_Display #(.active("false")) u_7_segment_display_2 (
    .g(Decodificador_0_9_2_g), .f(Decodificador_0_9_2_f), .a(Decodificador_0_9_2_a_2),
    .b(Decodificador_0_9_2_b_2), .e(Decodificador_0_9_2_e), .d(Decodificador_0_9_2_d_2),
    .c(Decodificador_0_9_2_c_2), .dp(Decodificador_0_9_2_dp));
endmodule

module decod_num_0_9 (
  input  a,
  input  b,
  input  c,
  input  d,
  output A_2,
  output B_2,
  output C_2,
  output D_2,
  output E,
  output F,
  output G,
  output DP
);

  wire and_1_out, and_2_out, and_3_out, and_4_out, and_5_out, and_6_out, and_7_out, and_8_out, and_9_out,
       and_10_out, and_11_out, and_12_out, and_13_out, and_14_out, and_15_out, and_16_out, and_17_out,
       and_18_out, and_19_out, and_20_out, and_21_out, and_22_out, and_23_out, and_24_out, and_25_out,
       and_26_out, not_1_out, not_2_out, not_3_out, not_4_out, not_5_out, not_6_out, not_7_out, not_8_out,
       not_9_out, not_10_out, not_11_out, not_12_out, not_13_out, not_14_out, not_15_out, not_16_out,
       not_17_out, not_18_out, not_19_out, not_20_out, not_21_out;

  not not_1 (not_1_out, a);
  not not_2 (not_2_out, b);
  not not_3 (not_3_out, c);
  not not_4 (not_4_out, c);
  not not_5 (not_5_out, d);
  and and_1 (and_1_out, a, b);
  and and_2 (and_2_out, a, c);
  and and_3 (and_3_out, b, c, not_6_out);
  not not_6 (not_6_out, d);
  not not_7 (not_7_out, c);
  and and_4 (and_4_out, b, not_7_out, d);
  and and_5 (and_5_out, a, b);
  and and_6 (and_6_out, a, c);
  not not_8 (not_8_out, b);
  and and_7 (and_7_out, not_8_out, c, not_9_out);
  not not_9 (not_9_out, d);
  not not_10 (not_10_out, a);
  not not_11 (not_11_out, b);
  not not_12 (not_12_out, c);
  not not_13 (not_13_out, c);
  not not_14 (not_14_out, d);
  and and_8 (and_8_out, a, c);
  and and_9 (and_9_out, b, not_15_out);
  not not_15 (not_15_out, c);
  and and_10 (and_10_out, a, b);
  not not_16 (not_16_out, a);
  and and_11 (and_11_out, not_16_out, not_17_out, d);
  not not_17 (not_17_out, b);
  not not_18 (not_18_out, b);
  and and_12 (and_12_out, not_18_out, c);
  and and_13 (and_13_out, c, d);
  and and_14 (and_14_out, a, b);
  and and_15 (and_15_out, a, c);
  not not_19 (not_19_out, a);
  not not_20 (not_20_out, b);
  and and_16 (and_16_out, not_19_out, not_20_out, not_21_out);
  not not_21 (not_21_out, c);
  and and_17 (and_17_out, b, c, d);
  and and_18 (and_18_out, a, b);
  and and_19 (and_19_out, a, c);
  and and_20 (and_20_out, not_1_out, not_2_out, not_3_out, d);
  and and_21 (and_21_out, b, not_4_out, not_5_out);
  or or_1 (B_2, and_1_out, and_2_out, and_3_out, and_4_out);
  or or_2 (C_2, and_5_out, and_6_out, and_7_out);
  and and_22 (and_22_out, a, b);
  and and_23 (and_23_out, a, c);
  and and_24 (and_24_out, not_10_out, not_11_out, not_12_out, d);
  and and_25 (and_25_out, b, c, d);
  and and_26 (and_26_out, b, not_13_out, not_14_out);
  or or_3 (E, and_8_out, and_9_out, d);
  or or_4 (F, and_10_out, and_11_out, and_12_out, and_13_out);
  or or_5 (G, and_14_out, and_15_out, and_16_out, and_17_out);
  or or_6 (A_2, and_18_out, and_19_out, and_20_out, and_21_out);
  or or_7 (D_2, and_22_out, and_23_out, and_24_out, and_25_out, and_26_out);

  assign DP = 1'b1;
endmodule
